# Fritzing sketch pcb_design (saved by Fritzing 0.9.3b)
breadboards: 1

parts:
  S1 = Pushbutton [package="[THT]"]
  S2 = Pushbutton [package="[THT]"]
  S3 = Pushbutton [package="[THT]"]
  S4 = Pushbutton [package="[THT]"]
  S5 = Pushbutton [package="[THT]"]
  S6 = Pushbutton [package="[THT]"]
  S7 = Pushbutton [package="[THT]"]
  S8 = Pushbutton [package="[THT]"]
  S9 = Pushbutton [package="[THT]"]
  S10 = Pushbutton [package="[THT]"]
  S11 = Pushbutton [package="[THT]"]
  S12 = Pushbutton [package="[THT]"]
  Part1 = Arduino Nano (Rev3.0)

nets:
  N1: S1.Pin_1, S1.Pin_2, S2.Pin_1, S2.Pin_2, S3.Pin_1, S3.Pin_2, S4.Pin_1, S4.Pin_2, S5.Pin_1, S5.Pin_2, S6.Pin_1, S6.Pin_2, Part1.5V
  N2: S1.Pin_3, S1.Pin_4
  N3: S2.Pin_3, S2.Pin_4
  N4: S3.Pin_3, S3.Pin_4
  N5: S4.Pin_3, S4.Pin_4
  N6: S5.Pin_3, S5.Pin_4
  N7: S6.Pin_3, S6.Pin_4
  N8: S7.Pin_1, S7.Pin_2, S8.Pin_1, S8.Pin_2, S9.Pin_1, S9.Pin_2, S10.Pin_1, S10.Pin_2, S11.Pin_1, S11.Pin_2, S12.Pin_1, S12.Pin_2, Part1.A1
  N9: S7.Pin_3, S7.Pin_4
  N10: S8.Pin_3, S8.Pin_4
  N11: S9.Pin_3, S9.Pin_4
  N12: S10.Pin_3, S10.Pin_4
  N13: S11.Pin_3, S11.Pin_4
  N14: S12.Pin_3, S12.Pin_4
