# Fritzing sketch pcb_design_one_sided (saved by Fritzing 0.9.3b)
circuit board: 14.32cm x 5.86968cm
breadboards: 1

parts:
  S2 = Pushbutton [package="[THT]"]
  S3 = Pushbutton [package="[THT]"]
  S4 = Pushbutton [package="[THT]"]
  S5 = Pushbutton [package="[THT]"]
  S6 = Pushbutton [package="[THT]"]
  S7 = Pushbutton [package="[THT]"]
  S8 = Pushbutton [package="[THT]"]
  S9 = Pushbutton [package="[THT]"]
  S10 = Pushbutton [package="[THT]"]
  S11 = Pushbutton [package="[THT]"]
  S12 = Pushbutton [package="[THT]"]
  R1 = Resistor [tolerance=±5% resistance=1k package=THT]
  R2 = Resistor [tolerance=±5% resistance=1.2k package=THT]
  R3 = Resistor [tolerance=±5% resistance=1.6k package=THT]
  R4 = Resistor [tolerance=±5% resistance=1.8k package=THT]
  R5 = Resistor [tolerance=±5% resistance=2.2k package=THT]
  R6 = Resistor [tolerance=±5% resistance=2.6k package=THT]
  R7 = Resistor [tolerance=±5% resistance=1k package=THT]
  R8 = Resistor [tolerance=±5% resistance=1.2k package=THT]
  R9 = Resistor [tolerance=±5% resistance=1.6k package=THT]
  R10 = Resistor [tolerance=±5% resistance=1.8k package=THT]
  R11 = Resistor [tolerance=±5% resistance=2.2k package=THT]
  R12 = Resistor [tolerance=±5% resistance=2.6k package=THT]
  Part1 = Arduino Nano (Rev3.0)
  R13 = Resistor [tolerance=±5% resistance=10k package=THT]
  R14 = Resistor [tolerance=±5% resistance=10k package=THT]
  S1 = Pushbutton [package="[THT]"]

nets (from the pcb view):
  N1: S2.Pin_1, S2.Pin_2, S3.Pin_1, S3.Pin_2, S4.Pin_1, S4.Pin_2, S5.Pin_1, S5.Pin_2, S6.Pin_1, S6.Pin_2, Part1.A0, R13.Pin_0, S1.Pin_1, S1.Pin_2
  N2: S2.Pin_3, S2.Pin_4, R2.Pin_0
  N3: S3.Pin_3, S3.Pin_4, R3.Pin_0
  N4: S4.Pin_3, S4.Pin_4, R4.Pin_0
  N5: S5.Pin_3, S5.Pin_4, R5.Pin_0
  N6: S6.Pin_3, S6.Pin_4, R6.Pin_0
  N7: S7.Pin_1, S7.Pin_2, S8.Pin_1, S8.Pin_2, S9.Pin_1, S9.Pin_2, S10.Pin_1, S10.Pin_2, S11.Pin_1, S11.Pin_2, S12.Pin_1, S12.Pin_2, Part1.A1, R14.Pin_1
  N8: S7.Pin_3, S7.Pin_4, R7.Pin_1
  N9: S8.Pin_3, S8.Pin_4, R8.Pin_1
  N10: S9.Pin_3, S9.Pin_4, R9.Pin_1
  N11: S10.Pin_3, S10.Pin_4, R10.Pin_1
  N12: S11.Pin_3, S11.Pin_4, R11.Pin_1
  N13: S12.Pin_3, S12.Pin_4, R12.Pin_1
  N14: R1.Pin_0, S1.Pin_3, S1.Pin_4
  N15: R1.Pin_1, R2.Pin_1, R3.Pin_1, R4.Pin_1, R5.Pin_1, R6.Pin_1, R7.Pin_0, R8.Pin_0, R9.Pin_0, R10.Pin_0, R11.Pin_0, R12.Pin_0, Part1.5V
  N16: Part1.GND, R13.Pin_1, R14.Pin_0
